# Fritzing sketch clock module (saved by Fritzing 1.0.3b)
circuit board: 6.88185cm x 3.8982cm
breadboards: 1

parts:
  Mod1 = Raspberry Pi Pico
  J3 = Camdenboss CTB0158-2 [part_number=CTB0158-2 package=THT]
  ZS-042_RTC1 = ZS-042 RTC Module
  RE1 = Rotary Encoder [package=THT]
  R8 = Resistor [tolerance=±5% power=0.25W resistance=10k package=THT]
  R9 = Resistor [tolerance=±5% power=0.25W resistance=10k package=THT]
  R10 = Resistor [tolerance=±5% power=0.25W resistance=10k package=THT]
  R12 = Resistor [tolerance=±5% power=0.25W resistance=4.7k package=THT]
  J4 = male pin header, 4 pins [form="♂ (male)" part_number="JST XH"]
  V4 = DC Power [voltage=5V internal_resistance=0.1Ω]
  R13 = Resistor [tolerance=±5% power=0.25W resistance=4.7k package=THT]
  J5 = female pin header, 4 pins [form="♀ (female)"]

nets:
  N1: Mod1.pin_3, Mod1.pin_8, Mod1.pin_13, Mod1.pin_18, Mod1.pin_23, Mod1.pin_28, Mod1.pin_33, Mod1.pin_38, Mod1.pin_42, J3.pin2, ZS-042_RTC1.GND, RE1.EncoderPinC, RE1.SwitchPinE, J4.pin1, V4.V-, J5.pin1
  N2: Mod1.pin_21, J4.pin3, R13.Pin_0
  N3: Mod1.pin_22, R12.Pin_0, J4.pin4
  N4: Mod1.pin_24, ZS-042_RTC1.SDA
  N5: Mod1.pin_25, ZS-042_RTC1.SCL
  N6: Mod1.pin_31, RE1.SwitchrPinD, R10.Pin_0, J5.pin3
  N7: Mod1.pin_32, RE1.EncoderPinB, R8.Pin_0, J5.pin4
  N8: Mod1.pin_34, RE1.EncoderPinA, R9.Pin_0, J5.pin2
  N9: Mod1.pin_36, ZS-042_RTC1.VCC, R8.Pin_1, R9.Pin_1, R10.Pin_1, R12.Pin_1, J4.pin2, R13.Pin_1
  N10: Mod1.pin_39, J3.pin1

notes:
  I2C connection to nixie controllers

custom parts:
  Raspberry Pi Pico: Raspberry Pi Pico. Based around the RP2040 microcontroller the Pico is a low cost microcontroller device bringing Raspberry Pi quality, cost, and easy of use to the microcontroller space. Jan 2021, Split part in to two versions: tht (this one) and SMD. This one will drill holes for a .1 in header in pcb to allow plugging in the module as well as providing pads to solder the module to the top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
  Rotary Encoder: Rotary Encoder from ALPSec11e with switch.
