# Fritzing sketch dc-booster (saved by Fritzing 1.0.3b)
circuit board: 4.93817cm x 4.58494cm
breadboards: 1

parts:
  C1 = Electrolytic Capacitor [capacitance=0.33mF voltage=35V package="100 mil [THT, electrolytic]"]
  C2 = Ceramic Capacitor [capacitance=2.2nF voltage=35V package="100 mil [THT, multilayer]"]
  R1 = Resistor [tolerance=±5% power=0.25W resistance=10k package=THT]
  R2 = Resistor [tolerance=±5% power=0.25W resistance=56k package=THT]
  R3 = Resistor [tolerance=±5% power=0.25W resistance=1k package=THT]
  D1 = Rectifier Diode [part_number=uf4004 package="300 mil [THT]"]
  Q1 = MOSFET-NCHANNEL [package=to220v]
  Q2 = NPN-Transistor [part_number=BC547 package="TO92 [THT]"]
  C3 = Ceramic Capacitor [capacitance=100pF voltage=35V package="100 mil [THT, multilayer]"]
  C4 = Electrolytic Capacitor [capacitance=2.2µF voltage=250V package="100 mil [THT, electrolytic]"]
  R4 = Resistor [tolerance=±5% power=0.25W resistance=470 package=THT]
  R5 = Resistor [tolerance=±5% power=0.25W resistance=220k package=THT]
  R6 = Resistor [tolerance=±5% power=0.25W resistance=2.2k package=THT]
  R7 = Trimmer Potentiometer [maximum_resistance=1kΩ knob_status=50% power=0.5W package=THT]
  J1 = Camdenboss CTB0158-2 [part_number=CTB0158-2 package=THT]
  J2 = Camdenboss CTB0158-2 [part_number=CTB0158-2 package=THT]
  L2 = Power Inductor [part_number=100uH package=DIP]
  U1 = 555 Timer [package="DIP8 [THT]"]

nets:
  GND: C1.-, C2.0, Q1.S, Q2.C, C3.0, C4.-, R4.Pin_1, J1.pin2, J2.pin2, U1.Ground
  12V: C1.+, R2.Pin_0, R3.Pin_0, J2.pin1, L2.2, U1.Reset, U1.Vcc_Supply_Voltage
  N1: C2.1, R1.Pin_1, U1.Trigger, U1.Threshold
  N2: R1.Pin_0, R3.Pin_1, U1.Discharge
  N3: R2.Pin_1, Q2.E, U1.Control_Voltage
  170V: D1.cathode, C4.+, R5.Pin_1, J1.pin1
  N4: D1.anode, Q1.D, R6.Pin_1, L2.1
  N5: Q1.G, U1.Output
  N6: Q2.B, R7.wiper
  N7: C3.1, R6.Pin_0
  N8: R4.Pin_0, R7.leg2
  N9: R5.Pin_0, R7.leg1

notes:
  Vout (power for nixie)
  Vin

custom parts:
  Power Inductor: Power Inductor. DIP.
