# Fritzing sketch pcb_schema (saved by Fritzing 0.9.10b)
circuit board: 3.9cm x 7.9cm
breadboards: 2

parts:
  IN12A1 = IN12A [part_number=IN12A]
  MSPA42 = TRANSISTOR_NPN [package=to-92-ammo]
  MSPA43 = TRANSISTOR_NPN [package=to-92-ammo]
  MSPA44 = TRANSISTOR_NPN [package=to-92-ammo]
  MSPA45 = TRANSISTOR_NPN [package=to-92-ammo]
  MSPA46 = TRANSISTOR_NPN [package=to-92-ammo]
  MSPA47 = TRANSISTOR_NPN [package=to-92-ammo]
  MSPA48 = TRANSISTOR_NPN [package=to-92-ammo]
  MSPA49 = TRANSISTOR_NPN [package=to-92-ammo]
  MSPA50 = TRANSISTOR_NPN [package=to-92-ammo]
  MSPA51 = TRANSISTOR_NPN [package=to-92-ammo]
  MSPA52 = TRANSISTOR_NPN [package=to-92-ammo]
  IC1 = MCP23017 I2C I/O Expander
  J1 = male pin header, 3 pins [form="♂ (male)"]
  J3 = male pin header, 3 pins [form="♂ (male)"]
  J5 = Screw terminal - 2 pins [package=THT]
  R7 = Resistor [tolerance=±5% resistance=15k power=0.25 package=THT]
  R6 = Resistor [tolerance=±5% resistance=15k power=0.25 package=THT]
  R5 = Resistor [tolerance=±5% resistance=15k power=0.25 package=THT]
  R4 = Resistor [tolerance=±5% resistance=15k power=0.25 package=THT]
  R3 = Resistor [tolerance=±5% resistance=15k power=0.25 package=THT]
  R2 = Resistor [tolerance=±5% resistance=15k power=0.25 package=THT]
  R8 = Resistor [tolerance=±5% resistance=15k power=0.25 package=THT]
  R9 = Resistor [tolerance=±5% resistance=15k power=0.25 package=THT]
  R0 = Resistor [tolerance=±5% resistance=15k power=0.25 package=THT]
  R1 = Resistor [tolerance=±5% resistance=15k power=0.25 package=THT]
  RNC = Resistor [tolerance=±5% resistance=15k power=0.25 package=THT]
  R12 = Resistor [tolerance=±5% resistance=22000 power=0.25 package=THT]
  J2 = male pin header, 3 pins [form="♂ (male)"]
  I2C_1 = Qwiic Connector
  I2C_2 = Qwiic Connector

nets:
  N1: IN12A1.pin1, MSPA43.C
  N2: IN12A1.pin2, MSPA44.C
  N3: IN12A1.pin3, MSPA42.C
  N4: IN12A1.pin4, MSPA46.C
  N5: IN12A1.pin5, MSPA47.C
  N6: IN12A1.pin6, MSPA52.C
  N7: IN12A1.pin7, MSPA45.C
  N8: IN12A1.pin8, MSPA51.C
  N9: IN12A1.pin9, MSPA50.C
  N10: IN12A1.pin0, MSPA49.C
  N11: IN12A1.pinAnode, R12.Pin_1
  N12: IN12A1.pinNC, MSPA48.C
  N13: MSPA42.E, MSPA43.E, MSPA44.E, MSPA45.E, MSPA46.E, MSPA47.E, MSPA48.E, MSPA49.E, MSPA50.E, MSPA51.E, MSPA52.E, J5.pin2
  N14: MSPA42.B, R3.Pin_0
  N15: MSPA43.B, R1.Pin_0
  N16: MSPA44.B, R2.Pin_0
  N17: MSPA45.B, R7.Pin_0
  N18: MSPA46.B, R4.Pin_0
  N19: MSPA47.B, R5.Pin_0
  N20: MSPA48.B, RNC.Pin_0
  N21: MSPA49.B, R0.Pin_0
  N22: MSPA50.B, R9.Pin_0
  N23: MSPA51.B, R8.Pin_0
  N24: MSPA52.B, R6.Pin_0
  N25: IC1.GPB0, R8.Pin_1
  N26: IC1.GPB1, R9.Pin_1
  N27: IC1.GPB2, R7.Pin_1
  N28: IC1.VDD, IC1.RESET, J1.pin3, J3.pin3, J2.pin3, I2C_1.SIG, I2C_2.SIG
  GND: IC1.VSS, J1.pin1, J3.pin1, J2.pin1, I2C_1.GND, I2C_2.GND
  N29: IC1.SCL, I2C_1.NC, I2C_2.NC
  VCC: IC1.SDA, I2C_1.VCC, I2C_2.VCC
  N30: IC1.A0, J3.pin2
  N31: IC1.A1, J2.pin2
  N32: IC1.A2, J1.pin2
  N33: IC1.GPA0, R4.Pin_1
  N34: IC1.GPA1, R5.Pin_1
  N35: IC1.GPA2, R3.Pin_1
  N36: IC1.GPA3, R2.Pin_1
  N37: IC1.GPA4, R1.Pin_1
  N38: IC1.GPA5, R6.Pin_1
  N39: IC1.GPA6, RNC.Pin_1
  N40: IC1.GPA7, R0.Pin_1
  N41: J5.pin1, R12.Pin_0

custom parts:
  IN12A: A 12pin IN12A Nixie Tube
  MCP23017 I2C I/O Expander: The MCP23017 uses two i2c pins (these can be shared with other i2c devices), and in exchange gives you 16 general purpose pins. You can set each of 16 pins to be input, output, input with a pullup or open drain. There's even the ability to get an interrupt via an external pin when any of the inputs change so you don't have to keep polling the chip.
  Qwiic Connector: Qwiic PCB connector
